// Logisim project tp2 structure S2.circ as structural Verilog: 2 circuits, main circuit main
module main (
  input  E0,
  input  E1,
  input  E2,
  input  E3
);

  wire \décodeur_1_a , \décodeur_1_b , \décodeur_1_c , \décodeur_1_d , \décodeur_1_e , \décodeur_1_f ,
       \décodeur_1_g ;

  \décodeur  \décodeur_1  (
    .a(\décodeur_1_a ), .b(\décodeur_1_b ), .c(\décodeur_1_c ), .d(\décodeur_1_d ), .e(\décodeur_1_e ),
    .f(\décodeur_1_f ), .g(\décodeur_1_g ), .E3(E3), .E2(E2), .E1(E1), .E0(E0));
  _7_Segment_Display u_7_segment_display_1 (
    .g(\décodeur_1_g ), .f(\décodeur_1_f ), .a(\décodeur_1_a ), .b(\décodeur_1_b ), .e(\décodeur_1_e ),
    .d(\décodeur_1_d ), .c(\décodeur_1_c ));  // open: dp
endmodule

module \décodeur  (
  input  E3,
  input  E2,
  input  E1,
  input  E0,
  output a,
  output b,
  output c,
  output d,
  output e,
  output f,
  output g
);

  wire and_1_out, and_2_out, and_3_out, and_4_out, and_5_out, and_6_out, and_7_out, and_8_out, and_9_out,
       and_10_out, and_11_out, and_12_out, not_1_out, not_2_out, not_3_out, not_4_out;

  not not_1 (not_1_out, E3);
  not not_2 (not_2_out, E2);
  not not_3 (not_3_out, E1);
  not not_4 (not_4_out, E0);
  and and_1 (and_1_out, E2, E0);
  and and_2 (and_2_out, not_2_out, not_4_out);
  and and_3 (and_3_out, not_4_out, not_3_out);
  and and_4 (and_4_out, E1, E2);
  or or_1 (c, E3, not_3_out, E0);
  and and_5 (and_5_out, not_4_out, not_2_out);
  and and_6 (and_6_out, E3, not_4_out);
  and and_7 (and_7_out, E1, not_2_out);
  and and_8 (and_8_out, not_2_out, not_4_out);
  and and_9 (and_9_out, E3, not_4_out);
  and and_10 (and_10_out, not_3_out, not_4_out);
  and and_11 (and_11_out, E3, E1);
  and and_12 (and_12_out, E0, E2);
  or or_2 (a, and_1_out, and_2_out, E1);
  or or_3 (b, and_3_out, and_4_out, not_1_out);
  or or_4 (d, and_5_out, and_6_out, and_7_out);
  or or_5 (e, and_8_out, and_9_out);
  or or_6 (f, and_10_out, and_11_out);
  or or_7 (g, and_12_out, E1);
endmodule
